# Fritzing sketch FritzingSchematic (saved by Fritzing 0.9.0b)

parts:
  Part1 = Electric Imp April
  U1 = RELAY [package=relay-g5q]
  S1 = Square Pushbutton

nets:
  N1: Part1.5, S1.leg0
  N2: Part1.6, U1.COIL2
  N3: Part1.9, U1.COIL1
  N4: Part1.13, Part1.14

notes:
  Existing Pushbutton
  Leads to door opener

custom parts:
  Electric Imp April: Electric Imp Breakout Board with onboard 3.3V regulated power supply
